// Logisim project 1-03-18.circ as structural Verilog: 1 circuit, main circuit main
module main (
  input  in_1,
  input  in_2,
  input  in_3,
  input  in_4,
  input  in_5,
  input  in_6,
  input  in_7,
  input  in_8,
  input  in_9,
  output out_10,
  output out_11,
  output NAND,
  output out_13
);

  wire multiplexer_2_out, not_1_out, undriven;

  not not_1 (not_1_out, in_1);
  Multiplexer multiplexer_1 (.in0(not_1_out), .in1(1'b0), .out(out_10), .sel(in_2));  // open: en
  Multiplexer multiplexer_2 (.in0(1'b0), .in1(in_7), .out(multiplexer_2_out), .sel(in_8), .en(undriven));
  not not_2 (NAND, multiplexer_2_out);
  Multiplexer multiplexer_3 (.in0(1'b0), .in1(in_3), .out(out_11), .sel(in_4), .en(in_5));
  Multiplexer multiplexer_4 (.in0(in_6), .in1(1'b1), .out(out_13), .sel(in_9));  // open: en

  // Notes on the sheet:
  //   NOR
  //   AND
  //   OR
endmodule
