// Logisim project 4 bit binary adder.circ as structural Verilog: 1 circuit, main circuit main
module main (
  input  [3:0] in_1,
  input  Cin,
  input  [3:0] in_3,
  output [3:0] out_4
);

  wire and_1_out, and_2_out, and_3_out, and_4_out, and_5_out, and_6_out, and_7_out, and_8_out, or_1_out,
       or_2_out, or_3_out, or_4_out, xor_1_out, xor_2_out, xor_5_out, xor_6_out;

  and and_1 (and_1_out, in_1[0], in_3[0]);
  and and_2 (and_2_out, in_1[1], in_3[1]);
  xor xor_1 (xor_1_out, in_1[0], in_3[0]);
  xor xor_2 (xor_2_out, in_1[1], in_3[1]);
  xor xor_3 (out_4[0], xor_1_out, Cin);
  and and_3 (and_3_out, Cin, xor_1_out);
  xor xor_4 (out_4[1], xor_2_out, or_1_out);
  and and_4 (and_4_out, or_1_out, xor_2_out);
  or or_1 (or_1_out, and_3_out, and_1_out);
  or or_2 (or_2_out, and_4_out, and_2_out);
  xor xor_5 (xor_5_out, in_1[2], in_3[2]);
  and and_5 (and_5_out, in_1[2], in_3[2]);
  xor xor_6 (xor_6_out, in_1[3], in_3[3]);
  and and_6 (and_6_out, in_1[3], in_3[3]);
  xor xor_7 (out_4[2], xor_5_out, or_2_out);
  and and_7 (and_7_out, or_2_out, xor_5_out);
  xor xor_8 (out_4[3], xor_6_out, or_3_out);
  and and_8 (and_8_out, or_3_out, xor_6_out);
  or or_3 (or_3_out, and_7_out, and_5_out);
  or or_4 (or_4_out, and_8_out, and_6_out);
  LED led_1 (.in(or_4_out));

  // Notes on the sheet:
  //   A0
  //   B0
  //   B1
  //   Cin
  //   S
  //   S
  //   C1
  //   C2
  //   A2
  //   A3
  //   B3
  //   S
  //   S
  //   C3
  //   C4t
endmodule
