// Logisim project Final.circ as structural Verilog: 1 circuit, main circuit main
module main (
  input  in_1,
  input  [3:0] in_2,
  input  [3:0] in_3,
  input  [3:0] in_4,
  input  [3:0] in_5,
  input  [1:0] in_6,
  input  [3:0] in_7,
  input  in_8,
  input  [3:0] in_9,
  input  [3:0] in_10,
  output [3:0] out_11
);

  wire [3:0] main_1_out_4, main_2_out_3, main_3_out_3, main_4_out_2;

  _4_bit_binary_adder_main main_1 (.in_1(in_2), .Cin(in_1), .in_3(in_3), .out_4(main_1_out_4));
  AND_main main_2 (.in_1(in_4), .in_2(in_5), .out_3(main_2_out_3));
  XOR_main main_3 (.in_1(in_7), .in_2(in_9), .out_3(main_3_out_3));
  NOT_main main_4 (.in_1(in_10), .out_2(main_4_out_2));
  MUX_main main_5 (
    .in_1(main_1_out_4), .in_2(main_2_out_3), .in_3(main_3_out_3), .in_4(main_4_out_2), .in_5(in_8),
    .in_6(in_6), .out_7(out_11));

  // Notes on the sheet:
  //   AND
  //   XOR
  //   Adder
  //   NOT
endmodule
