// Logisim project MUX.circ as structural Verilog: 1 circuit, main circuit main
module main (
  input  [3:0] in_1,
  input  [3:0] in_2,
  input  [3:0] in_3,
  input  [3:0] in_4,
  input  in_5,
  input  [1:0] in_6,
  output [3:0] out_7
);

  wire decoder_1_out0, decoder_1_out1, decoder_1_out2, decoder_1_out3;

  Decoder #(.select(2)) decoder_1 (
    .out0(decoder_1_out0), .out1(decoder_1_out1), .out2(decoder_1_out2), .out3(decoder_1_out3), .sel(in_6),
    .en(in_5));
  assign out_7 = decoder_1_out0 ? in_1 : 4'bz;  // Controlled_Buffer controlled_buffer_1
  assign out_7 = decoder_1_out1 ? in_2 : 4'bz;  // Controlled_Buffer controlled_buffer_2
  assign out_7 = decoder_1_out2 ? in_3 : 4'bz;  // Controlled_Buffer controlled_buffer_3
  assign out_7 = decoder_1_out3 ? in_4 : 4'bz;  // Controlled_Buffer controlled_buffer_4
endmodule
