// Logisim project ringcounter.circ as structural Verilog: 1 circuit, main circuit main
module main (
  input  in_1,
  input  in_2
);

  wire clock_1_out, clock_2_out, d_ff_1_q, d_ff_2_q, d_ff_3_q, d_ff_4_q, d_ff_5_q, d_ff_6_q, d_ff_7_q,
       d_ff_8_q;

  Clock clock_1 (.out(clock_1_out));
  Clock clock_2 (.out(clock_2_out));
  D_Flip_Flop d_ff_1 (.clk(clock_1_out), .D(d_ff_7_q), .Q(d_ff_1_q), .reset(in_1));  // open: Qn, preset, en
  D_Flip_Flop d_ff_2 (.clk(clock_2_out), .D(d_ff_8_q), .Q(d_ff_2_q), .reset(in_2));  // open: Qn, preset, en
  D_Flip_Flop d_ff_3 (.clk(clock_1_out), .D(d_ff_1_q), .Q(d_ff_3_q), .reset(in_1));  // open: Qn, preset, en
  D_Flip_Flop d_ff_4 (.clk(clock_2_out), .D(d_ff_2_q), .Q(d_ff_4_q), .reset(in_2));  // open: Qn, preset, en
  D_Flip_Flop d_ff_5 (.clk(clock_1_out), .D(d_ff_3_q), .Q(d_ff_5_q), .reset(in_1));  // open: Qn, preset, en
  D_Flip_Flop d_ff_6 (.clk(clock_2_out), .D(d_ff_4_q), .Q(d_ff_6_q), .reset(in_2));  // open: Qn, preset, en
  D_Flip_Flop d_ff_7 (.clk(clock_1_out), .D(d_ff_5_q), .Q(d_ff_7_q), .reset(in_1));  // open: Qn, preset, en
  D_Flip_Flop d_ff_8 (.clk(clock_2_out), .D(d_ff_6_q), .Q(d_ff_8_q), .reset(in_2));  // open: Qn, preset, en

  // Notes on the sheet:
  //   QA
  //   QB
  //   QC
  //   QD
endmodule
