// Logisim project twos complement adder.circ as structural Verilog: 1 circuit, main circuit main
module main (
  input  [3:0] in_1,
  input  M,
  input  [3:0] in_3,
  output out_4,
  output [3:0] out_5
);

  wire main_1_c1, main_2_c1, main_3_c1, main_4_c1, xor_1_out, xor_3_out, xor_4_out, xor_5_out;

  xor xor_1 (xor_1_out, in_1[3], M);
  _1_bit_binary_adder_main main_1 (.A0(in_3[3]), .B0(xor_1_out), .Cin(main_2_c1), .S(out_5[3]), .C1(main_1_c1));
  xor xor_2 (out_4, main_1_c1, main_2_c1);
  xor xor_3 (xor_3_out, in_1[2], M);
  _1_bit_binary_adder_main main_2 (.A0(in_3[2]), .B0(xor_3_out), .Cin(main_3_c1), .S(out_5[2]), .C1(main_2_c1));
  xor xor_4 (xor_4_out, in_1[1], M);
  _1_bit_binary_adder_main main_3 (.A0(in_3[1]), .B0(xor_4_out), .Cin(main_4_c1), .S(out_5[1]), .C1(main_3_c1));
  xor xor_5 (xor_5_out, in_1[0], M);
  _1_bit_binary_adder_main main_4 (.A0(in_3[0]), .B0(xor_5_out), .Cin(M), .S(out_5[0]), .C1(main_4_c1));

  // Notes on the sheet:
  //   A0
  //   B0
  //   C1
endmodule
